// Logisim project RISC-V DataPath.circ as structural Verilog: 14 circuits, main circuit RISC V single cycle core
module imm_gen (
  input  [31:0] inst,
  input  [31:0] PC,
  output [31:0] out_3,
  output [31:0] out_4,
  output [31:0] out_5,
  output [31:0] out_6,
  output [31:0] out_7
);

  wire [19:0] shifter_1_out;
  wire [31:0] bit_extender_3_out, bit_extender_4_out;

  assign out_3 = {{20{inst[31]}}, inst[31:20]};  // Bit_Extender bit_extender_1
  assign out_4 = {{20{inst[31]}}, {inst[31:25], inst[11:7]}};  // Bit_Extender bit_extender_2
  assign bit_extender_3_out = {{19{inst[31]}}, {inst[31], inst[7], inst[30:25], inst[11:8], 1'b0}};  // Bit_Extender bit_extender_3
  assign bit_extender_4_out = {{11{inst[31]}}, {inst[31], inst[19:12], inst[20], inst[30:21], 1'b0}};  // Bit_Extender bit_extender_4
  Shifter #(.width(20)) shifter_1 (.in(inst[31:12]), .\dist (5'b01100), .out(shifter_1_out));
  Adder #(.width(32)) adder_1 (.a(bit_extender_3_out), .b(PC), .out(out_5));  // open: cin, cout
  Adder #(.width(32)) adder_2 (.a(bit_extender_4_out), .b(PC), .out(out_6));  // open: cin, cout
  assign out_7 = {{12{shifter_1_out[19]}}, shifter_1_out};  // Bit_Extender bit_extender_5

  // Notes on the sheet:
  //   I-Type
  //   S-type
  //   Sb-Type
  //   UJ-Type
  //   U-Type
endmodule

module reg_file (
  input  [31:0] write_data,
  input  [4:0] rd,
  input  reg_enable,
  input  [4:0] rs1,
  input  [4:0] rs2,
  input  clock,
  output [31:0] A,
  output [31:0] B
);

  wire decoder_1_out1, decoder_1_out2, decoder_1_out3, decoder_1_out4, decoder_1_out5, decoder_1_out6,
       decoder_1_out7, decoder_1_out8, decoder_1_out9, decoder_1_out10, decoder_1_out11, decoder_1_out12,
       decoder_1_out13, decoder_1_out14, decoder_1_out15, decoder_1_out16, decoder_1_out17, decoder_1_out18,
       decoder_1_out19, decoder_1_out20, decoder_1_out21, decoder_1_out22, decoder_1_out23, decoder_1_out24,
       decoder_1_out25, decoder_1_out26, decoder_1_out27, decoder_1_out28, decoder_1_out29, decoder_1_out30,
       decoder_1_out31;
  wire [31:0] register_1_q, register_2_q, register_3_q, register_4_q, register_5_q, register_6_q,
       register_7_q, register_8_q, register_9_q, register_10_q, register_11_q, register_12_q, register_13_q,
       register_14_q, register_15_q, register_16_q, register_17_q, register_18_q, register_19_q,
       register_20_q, register_21_q, register_22_q, register_23_q, register_24_q, register_25_q,
       register_26_q, register_27_q, register_28_q, register_29_q, register_30_q, register_31_q;

  Decoder #(.select(5), .disabled(0)) decoder_1 (
    .out1(decoder_1_out1), .out2(decoder_1_out2), .out3(decoder_1_out3), .out4(decoder_1_out4),
    .out5(decoder_1_out5), .out6(decoder_1_out6), .out7(decoder_1_out7), .out8(decoder_1_out8),
    .out9(decoder_1_out9), .out10(decoder_1_out10), .out11(decoder_1_out11), .out12(decoder_1_out12),
    .out13(decoder_1_out13), .out14(decoder_1_out14), .out15(decoder_1_out15), .out16(decoder_1_out16),
    .out17(decoder_1_out17), .out18(decoder_1_out18), .out19(decoder_1_out19), .out20(decoder_1_out20),
    .out21(decoder_1_out21), .out22(decoder_1_out22), .out23(decoder_1_out23), .out24(decoder_1_out24),
    .out25(decoder_1_out25), .out26(decoder_1_out26), .out27(decoder_1_out27), .out28(decoder_1_out28),
    .out29(decoder_1_out29), .out30(decoder_1_out30), .out31(decoder_1_out31), .sel(rd), .en(reg_enable));  // open: out0
  Register #(.width(32)) register_1 (.D(write_data), .en(decoder_1_out1), .Q(register_1_q), .clk(clock));  // open: clr
  Register #(.width(32)) register_2 (.D(write_data), .en(decoder_1_out2), .Q(register_2_q), .clk(clock));  // open: clr
  Register #(.width(32)) register_3 (.D(write_data), .en(decoder_1_out3), .Q(register_3_q), .clk(clock));  // open: clr
  Register #(.width(32)) register_4 (.D(write_data), .en(decoder_1_out4), .Q(register_4_q), .clk(clock));  // open: clr
  Register #(.width(32)) register_5 (.D(write_data), .en(decoder_1_out5), .Q(register_5_q), .clk(clock));  // open: clr
  Register #(.width(32)) register_6 (.D(write_data), .en(decoder_1_out6), .Q(register_6_q), .clk(clock));  // open: clr
  Register #(.width(32)) register_7 (.D(write_data), .en(decoder_1_out7), .Q(register_7_q), .clk(clock));  // open: clr
  Register #(.width(32)) register_8 (.D(write_data), .en(decoder_1_out8), .Q(register_8_q), .clk(clock));  // open: clr
  Register #(.width(32)) register_9 (.D(write_data), .en(decoder_1_out9), .Q(register_9_q), .clk(clock));  // open: clr
  Register #(.width(32)) register_10 (
    .D(write_data), .en(decoder_1_out10), .Q(register_10_q), .clk(clock));  // open: clr
  Register #(.width(32)) register_11 (
    .D(write_data), .en(decoder_1_out11), .Q(register_11_q), .clk(clock));  // open: clr
  Register #(.width(32)) register_12 (
    .D(write_data), .en(decoder_1_out12), .Q(register_12_q), .clk(clock));  // open: clr
  Register #(.width(32)) register_13 (
    .D(write_data), .en(decoder_1_out13), .Q(register_13_q), .clk(clock));  // open: clr
  Register #(.width(32)) register_14 (
    .D(write_data), .en(decoder_1_out14), .Q(register_14_q), .clk(clock));  // open: clr
  Register #(.width(32)) register_15 (
    .D(write_data), .en(decoder_1_out15), .Q(register_15_q), .clk(clock));  // open: clr
  Register #(.width(32)) register_16 (
    .D(write_data), .en(decoder_1_out16), .Q(register_16_q), .clk(clock));  // open: clr
  Register #(.width(32)) register_17 (
    .D(write_data), .en(decoder_1_out17), .Q(register_17_q), .clk(clock));  // open: clr
  Register #(.width(32)) register_18 (
    .D(write_data), .en(decoder_1_out18), .Q(register_18_q), .clk(clock));  // open: clr
  Register #(.width(32)) register_19 (
    .D(write_data), .en(decoder_1_out19), .Q(register_19_q), .clk(clock));  // open: clr
  Register #(.width(32)) register_20 (
    .D(write_data), .en(decoder_1_out20), .Q(register_20_q), .clk(clock));  // open: clr
  Register #(.width(32)) register_21 (
    .D(write_data), .en(decoder_1_out21), .Q(register_21_q), .clk(clock));  // open: clr
  Register #(.width(32)) register_22 (
    .D(write_data), .en(decoder_1_out22), .Q(register_22_q), .clk(clock));  // open: clr
  Register #(.width(32)) register_23 (
    .D(write_data), .en(decoder_1_out23), .Q(register_23_q), .clk(clock));  // open: clr
  Register #(.width(32)) register_24 (
    .D(write_data), .en(decoder_1_out24), .Q(register_24_q), .clk(clock));  // open: clr
  Register #(.width(32)) register_25 (
    .D(write_data), .en(decoder_1_out25), .Q(register_25_q), .clk(clock));  // open: clr
  Register #(.width(32)) register_26 (
    .D(write_data), .en(decoder_1_out26), .Q(register_26_q), .clk(clock));  // open: clr
  Register #(.width(32)) register_27 (
    .D(write_data), .en(decoder_1_out27), .Q(register_27_q), .clk(clock));  // open: clr
  Register #(.width(32)) register_28 (
    .D(write_data), .en(decoder_1_out28), .Q(register_28_q), .clk(clock));  // open: clr
  Register #(.width(32)) register_29 (
    .D(write_data), .en(decoder_1_out29), .Q(register_29_q), .clk(clock));  // open: clr
  Register #(.width(32)) register_30 (
    .D(write_data), .en(decoder_1_out30), .Q(register_30_q), .clk(clock));  // open: clr
  Register #(.width(32)) register_31 (
    .D(write_data), .en(decoder_1_out31), .Q(register_31_q), .clk(clock));  // open: clr
  Multiplexer #(.select(5), .width(32)) multiplexer_1 (
    .in0({32{1'b0}}), .in1(register_1_q), .in2(register_2_q), .in3(register_3_q), .in4(register_4_q),
    .in5(register_5_q), .in6(register_6_q), .in7(register_7_q), .in8(register_8_q), .in9(register_9_q),
    .in10(register_10_q), .in11(register_11_q), .in12(register_12_q), .in13(register_13_q),
    .in14(register_14_q), .in15(register_15_q), .in16(register_16_q), .in17(register_17_q),
    .in18(register_18_q), .in19(register_19_q), .in20(register_20_q), .in21(register_21_q),
    .in22(register_22_q), .in23(register_23_q), .in24(register_24_q), .in25(register_25_q),
    .in26(register_26_q), .in27(register_27_q), .in28(register_28_q), .in29(register_29_q),
    .in30(register_30_q), .in31(register_31_q), .out(A), .sel(rs1));  // open: en
  Multiplexer #(.select(5), .width(32)) multiplexer_2 (
    .in0({32{1'b0}}), .in1(register_1_q), .in2(register_2_q), .in3(register_3_q), .in4(register_4_q),
    .in5(register_5_q), .in6(register_6_q), .in7(register_7_q), .in8(register_8_q), .in9(register_9_q),
    .in10(register_10_q), .in11(register_11_q), .in12(register_12_q), .in13(register_13_q),
    .in14(register_14_q), .in15(register_15_q), .in16(register_16_q), .in17(register_17_q),
    .in18(register_18_q), .in19(register_19_q), .in20(register_20_q), .in21(register_21_q),
    .in22(register_22_q), .in23(register_23_q), .in24(register_24_q), .in25(register_25_q),
    .in26(register_26_q), .in27(register_27_q), .in28(register_28_q), .in29(register_29_q),
    .in30(register_30_q), .in31(register_31_q), .out(B), .sel(rs2));  // open: en
endmodule

module control_decode (
  input  R_type,
  input  JALR,
  input  load,
  input  I_type,
  input  store,
  input  branch,
  input  LUI,
  input  AUIPC,
  input  JAL,
  input  [2:0] in_10,
  input  in_11,
  output REG_write,
  output Branch_2,
  output store_2,
  output Load_2,
  output mem2reg,
  output [1:0] OP_A_sel,
  output OP_B_SEL,
  output [1:0] IMM_sel,
  output [1:0] next_PC_SEL,
  output [3:0] ALU_CONTROL
);

  wire alu_op_1_out_0, alu_op_1_out_1, alu_op_1_out_3, or_1_out, or_2_out, or_4_out, or_5_out;

  or or_1 (or_1_out, JALR, load, I_type);
  or or_2 (or_2_out, AUIPC, LUI);
  or or_3 (REG_write, JAL, LUI, R_type, JALR, I_type, AUIPC, load);
  or or_4 (or_4_out, R_type, JALR, load, I_type, store, branch);
  or or_5 (or_5_out, JAL, JALR);
  or or_6 (OP_B_SEL, JALR, load, I_type, store, AUIPC, LUI);
  IMM_sel imm_sel_1 (.i(or_1_out), .s(store), .u(or_2_out), .A(IMM_sel[1]), .B(IMM_sel[0]));
  next_PC_sel next_pc_sel_1 (
    .branch(branch), .jal(JAL), .jalr(JALR), .A(next_PC_SEL[1]), .B(next_PC_SEL[0]));  // open: pc
  ALU_op alu_op_1 (
    .r(R_type), .i(I_type), .load(load), .jalr(JALR), .store(store), .AUIPC(AUIPC), .LUI(LUI), .JAL(JAL),
    .out_3(alu_op_1_out_3), .out_1(alu_op_1_out_1), .out_0(alu_op_1_out_0));
  op_A_select op_a_select_1 (.rs1(or_4_out), .pc(AUIPC), .pc4(or_5_out), .zero(1'b0), .a(OP_A_sel[1]), .b(OP_A_sel[0]));
  or or_7 (mem2reg, load, JALR);
  alu_control alu_control_1 (
    .aluop_2(alu_op_1_out_3), .aluop_1(alu_op_1_out_1), .aluop_0(alu_op_1_out_0), .func3_2(in_10[2]),
    .func3_1(in_10[1]), .func3_0(in_10[0]), .func7_30(in_11), .a(ALU_CONTROL[3]), .b(ALU_CONTROL[2]),
    .c(ALU_CONTROL[1]), .d(ALU_CONTROL[0]));

  assign Branch_2 = branch;
  assign Load_2 = load;
  assign store_2 = store;
endmodule

module ALU (
  input  [31:0] in_1,
  input  [31:0] in_2,
  input  [3:0] data_select,
  output [31:0] out_4
);

  wire comparator_1_lt, comparator_2_lt;
  wire [4:0] bit_extender_1_out, bit_extender_2_out, bit_extender_3_out;
  wire [31:0] adder_1_out, and_1_out, bit_extender_4_out, bit_extender_5_out, or_1_out, shifter_1_out,
       shifter_2_out, shifter_3_out, subtractor_1_out, xor_1_out;

  Bit_Extender #(.in_width(32), .out_width(5)) bit_extender_1 (.in(in_2), .out(bit_extender_1_out));
  Bit_Extender #(.in_width(32), .out_width(5)) bit_extender_2 (.in(in_2), .out(bit_extender_2_out));
  Bit_Extender #(.in_width(32), .out_width(5)) bit_extender_3 (.in(in_2), .out(bit_extender_3_out));
  Adder #(.width(32)) adder_1 (.a(in_1), .b(in_2), .out(adder_1_out), .cin(1'b0));  // open: cout
  Subtractor #(.width(32)) subtractor_1 (.a(in_1), .b(in_2), .out(subtractor_1_out), .bin(1'b0));  // open: bout
  assign and_1_out = in_1 & in_2;  // AND_Gate and_1, 32 bits wide
  assign or_1_out = in_1 | in_2;  // OR_Gate or_1, 32 bits wide
  assign xor_1_out = in_1 ^ in_2;  // XOR_Gate xor_1, 32 bits wide
  Shifter #(.width(32)) shifter_1 (.in(in_1), .\dist (bit_extender_1_out), .out(shifter_1_out));
  Shifter #(.width(32), .shift("lr")) shifter_2 (.in(in_1), .\dist (bit_extender_2_out), .out(shifter_2_out));
  Comparator #(.width(32)) comparator_1 (.a(in_1), .b(in_2), .lt(comparator_1_lt));  // open: gt, eq
  Comparator #(.width(32), .mode("unsigned")) comparator_2 (.a(in_1), .b(in_2), .lt(comparator_2_lt));  // open: gt, eq
  Shifter #(.width(32), .shift("ar")) shifter_3 (.in(in_1), .\dist (bit_extender_3_out), .out(shifter_3_out));
  assign bit_extender_4_out = {{31{1'b0}}, comparator_1_lt};  // Bit_Extender bit_extender_4
  assign bit_extender_5_out = {{31{1'b0}}, comparator_2_lt};  // Bit_Extender bit_extender_5
  Multiplexer #(.select(4), .width(32)) multiplexer_1 (
    .in0(adder_1_out), .in1(subtractor_1_out), .in2(and_1_out), .in3(or_1_out), .in4(xor_1_out),
    .in5(shifter_1_out), .in6(shifter_2_out), .in7(bit_extender_4_out), .in8(bit_extender_5_out),
    .in9(shifter_3_out), .in15(in_1), .out(out_4), .sel(data_select));  // open: in10, in11, in12, in13, in14, en

  // Notes on the sheet:
  //   A
  //   B
  //   adder
  //   subtractor
  //   AND
  //   OR
  //   XOR
  //   sll
  //   srl
  //   slt
  //   sltu
  //   sra
endmodule

module control_unit (
  input  [6:0] in_1,
  input  [2:0] in_2,
  input  in_3,
  output reg_write,
  output branch,
  output store,
  output load,
  output mem2reg,
  output [1:0] op_A_sel,
  output op_B_sel,
  output [1:0] Imm_sel,
  output [1:0] nextPC_sel,
  output [3:0] ALU_control
);

  wire decoder_1_auipc, decoder_1_i_type, decoder_1_jalr, decoder_1_load, decoder_1_lui, decoder_1_r_type,
       decoder_1_s_type, decoder_1_sb_type, decoder_1_uj_type;

  decoder decoder_1 (
    .in_1(in_1), .R_Type(decoder_1_r_type), .jalr(decoder_1_jalr), .Load(decoder_1_load),
    .I_type(decoder_1_i_type), .S_Type(decoder_1_s_type), .Sb_type(decoder_1_sb_type), .LUI(decoder_1_lui),
    .AUIPC(decoder_1_auipc), .Uj_Type(decoder_1_uj_type));
  control_decode control_decode_1 (
    .REG_write(reg_write), .store_2(store), .Load_2(load), .mem2reg(mem2reg), .OP_A_sel(op_A_sel),
    .OP_B_SEL(op_B_sel), .IMM_sel(Imm_sel), .next_PC_SEL(nextPC_sel), .R_type(decoder_1_r_type),
    .JALR(decoder_1_jalr), .load(decoder_1_load), .I_type(decoder_1_i_type), .store(decoder_1_s_type),
    .branch(decoder_1_sb_type), .LUI(decoder_1_lui), .AUIPC(decoder_1_auipc), .JAL(decoder_1_uj_type),
    .in_10(in_2), .in_11(in_3), .ALU_CONTROL(ALU_control), .Branch_2(branch));

  // Notes on the sheet:
  //   control decode
endmodule

module IMM_sel (
  input  i,
  input  s,
  input  u,
  output A,
  output B
);

  wire and_1_out, and_2_out, and_3_out, and_4_out, not_1_out, not_2_out, not_3_out, not_4_out;

  not not_1 (not_1_out, i);
  not not_2 (not_2_out, s);
  not not_3 (not_3_out, i);
  not not_4 (not_4_out, u);
  and and_1 (and_1_out, not_1_out, not_2_out);
  and and_2 (and_2_out, i, s);
  and and_3 (and_3_out, not_3_out, not_4_out);
  and and_4 (and_4_out, i, u);
  or or_1 (A, and_1_out, u, and_2_out);
  or or_2 (B, and_3_out, s, and_4_out);
endmodule

module next_PC_sel (
  input  pc,
  input  branch,
  input  jal,
  input  jalr,
  output A,
  output B
);

  or or_1 (A, jalr, branch);
  or or_2 (B, jal, jalr);
endmodule

module ALU_op (
  input  r,
  input  i,
  input  load,
  input  jalr,
  input  store,
  input  AUIPC,
  input  LUI,
  input  JAL,
  output out_3,
  output out_1,
  output out_0
);

  or or_1 (out_3, JAL, LUI, AUIPC, store);
  or or_2 (out_1, JAL, LUI, jalr, load);
  or or_3 (out_0, JAL, AUIPC, jalr, i);
endmodule

module alu_control (
  input  aluop_2,
  input  aluop_1,
  input  aluop_0,
  input  func3_2,
  input  func3_1,
  input  func3_0,
  input  func7_30,
  output a,
  output b,
  output c,
  output d
);

  wire and_1_out, and_2_out, and_3_out, and_4_out, and_5_out, and_6_out, and_7_out, and_8_out, and_9_out,
       and_10_out, and_11_out, and_12_out, and_13_out, and_14_out, and_15_out, and_16_out, not_1_out,
       not_2_out, not_3_out, not_4_out, not_5_out, not_6_out, not_7_out, not_8_out, not_9_out, not_10_out,
       not_11_out, not_12_out, not_13_out, not_14_out, not_15_out, not_16_out, not_17_out, not_18_out,
       not_19_out, not_20_out, not_21_out, not_22_out, not_23_out, not_24_out, not_25_out, not_26_out,
       not_27_out, not_28_out, not_29_out, not_30_out, not_31_out;

  not not_1 (not_1_out, aluop_2);
  not not_2 (not_2_out, func3_1);
  not not_3 (not_3_out, aluop_2);
  not not_4 (not_4_out, func3_2);
  not not_5 (not_5_out, aluop_2);
  not not_6 (not_6_out, func3_1);
  not not_7 (not_7_out, func7_30);
  not not_8 (not_8_out, aluop_2);
  not not_9 (not_9_out, aluop_0);
  not not_10 (not_10_out, func3_2);
  not not_11 (not_11_out, func3_0);
  not not_12 (not_12_out, aluop_2);
  not not_13 (not_13_out, func3_1);
  not not_14 (not_14_out, func3_0);
  not not_15 (not_15_out, aluop_2);
  not not_16 (not_16_out, aluop_0);
  not not_17 (not_17_out, func3_0);
  not not_18 (not_18_out, aluop_2);
  not not_19 (not_19_out, func7_30);
  not not_20 (not_20_out, aluop_2);
  not not_21 (not_21_out, aluop_1);
  not not_22 (not_22_out, aluop_0);
  not not_23 (not_23_out, func3_1);
  not not_24 (not_24_out, aluop_2);
  not not_25 (not_25_out, func3_2);
  not not_26 (not_26_out, func3_1);
  not not_27 (not_27_out, aluop_2);
  not not_28 (not_28_out, func3_1);
  not not_29 (not_29_out, aluop_2);
  not not_30 (not_30_out, aluop_0);
  not not_31 (not_31_out, func3_0);
  and and_1 (and_1_out, not_1_out, not_2_out, func3_0, func7_30);
  and and_2 (and_2_out, not_3_out, not_4_out, func3_1, func3_0);
  and and_3 (and_3_out, aluop_1, aluop_0);
  and and_4 (and_4_out, not_5_out, not_6_out, func3_0, not_7_out);
  and and_5 (and_5_out, not_8_out, not_9_out, not_10_out, func3_1, not_11_out);
  and and_6 (and_6_out, not_12_out, func3_2, not_13_out, not_14_out);
  and and_7 (and_7_out, aluop_1, aluop_0);
  and and_8 (and_8_out, not_15_out, not_16_out, func3_1, not_17_out);
  and and_9 (and_9_out, not_18_out, func3_2, func3_0, not_19_out);
  and and_10 (and_10_out, not_20_out, func3_2, func3_1);
  and and_11 (and_11_out, aluop_1, aluop_0);
  and and_12 (and_12_out, not_21_out, not_22_out, not_23_out, func7_30);
  and and_13 (and_13_out, not_24_out, not_25_out, not_26_out, func3_0);
  and and_14 (and_14_out, not_27_out, not_28_out, func3_0, func7_30);
  and and_15 (and_15_out, not_29_out, not_30_out, func3_1, not_31_out);
  and and_16 (and_16_out, aluop_1, aluop_0);
  or or_1 (a, and_1_out, and_2_out, and_3_out);
  or or_2 (b, and_4_out, and_5_out, and_6_out, and_7_out);
  or or_3 (c, and_8_out, and_9_out, and_10_out, and_11_out);
  or or_4 (d, and_12_out, and_13_out, and_14_out, and_15_out, and_16_out);
endmodule

module op_A_select (
  input  rs1,
  input  pc,
  input  pc4,
  input  zero,
  output a,
  output b
);

  or or_1 (a, zero, pc4);
  or or_2 (b, zero, pc);
endmodule

module branch (
  input  [2:0] func_3,
  input  [31:0] in_2,
  input  [31:0] in_3,
  input  EN,
  output RESULT
);

  wire comparator_1_eq, comparator_2_eq, comparator_3_lt, comparator_4_eq, comparator_4_gt, comparator_5_lt,
       comparator_6_eq, comparator_6_gt, not_1_out, or_1_out, or_2_out;

  Comparator #(.width(32)) comparator_1 (.a(in_3), .b(in_2), .eq(comparator_1_eq));  // open: gt, lt
  Comparator #(.width(32)) comparator_2 (.a(in_3), .b(in_2), .eq(comparator_2_eq));  // open: gt, lt
  Comparator #(.width(32)) comparator_3 (.a(in_3), .b(in_2), .lt(comparator_3_lt));  // open: gt, eq
  Comparator #(.width(32)) comparator_4 (.a(in_3), .b(in_2), .gt(comparator_4_gt), .eq(comparator_4_eq));  // open: lt
  Comparator #(.width(32), .mode("unsigned")) comparator_5 (.a(in_3), .b(in_2), .lt(comparator_5_lt));  // open: gt, eq
  Comparator #(.width(32), .mode("unsigned")) comparator_6 (
    .a(in_3), .b(in_2), .gt(comparator_6_gt), .eq(comparator_6_eq));  // open: lt
  not not_1 (not_1_out, comparator_2_eq);
  or or_1 (or_1_out, comparator_4_gt, comparator_4_eq);
  or or_2 (or_2_out, comparator_6_gt, comparator_6_eq);
  Multiplexer #(.select(3)) multiplexer_1 (
    .in0(comparator_1_eq), .in1(not_1_out), .in4(comparator_3_lt), .in5(or_1_out), .in6(comparator_5_lt),
    .in7(or_2_out), .out(RESULT), .sel(func_3), .en(EN));  // open: in2, in3

  // Notes on the sheet:
  //   A
  //   B
  //   beq
  //   bne
  //   blt
  //   bge
  //   bltu
  //   bgeu
endmodule

module jalr (
  input  [31:0] rs1,
  input  [31:0] imm,
  output [31:0] target
);

  Adder #(.width(32)) adder_1 (.a(rs1), .b(imm), .out(target));  // open: cin, cout
endmodule

module decoder (
  input  [6:0] in_1,
  output R_Type,
  output jalr,
  output Load,
  output I_type,
  output S_Type,
  output Sb_type,
  output LUI,
  output AUIPC,
  output Uj_Type
);

  Comparator #(.width(7)) comparator_1 (.a(in_1), .b(7'b0110011), .eq(R_Type));  // open: gt, lt
  Comparator #(.width(7)) comparator_2 (.a(in_1), .b(7'b1100111), .eq(jalr));  // open: gt, lt
  Comparator #(.width(7)) comparator_3 (.a(in_1), .b(7'b0010011), .eq(Load));  // open: gt, lt
  Comparator #(.width(7)) comparator_4 (.a(in_1), .b(7'b0000011), .eq(I_type));  // open: gt, lt
  Comparator #(.width(7)) comparator_5 (.a(in_1), .b(7'b0100011), .eq(S_Type));  // open: gt, lt
  Comparator #(.width(7)) comparator_6 (.a(in_1), .b(7'b1100011), .eq(Sb_type));  // open: gt, lt
  Comparator #(.width(7)) comparator_7 (.a(in_1), .b(7'b0110111), .eq(LUI));  // open: gt, lt
  Comparator #(.width(7)) comparator_8 (.a(in_1), .b(7'b0010111), .eq(AUIPC));  // open: gt, lt
  Comparator #(.width(7)) comparator_9 (.a(in_1), .b(7'b1101111), .eq(Uj_Type));  // open: gt, lt
endmodule

module RISC_V_single_cycle_core (
  output [1:0] out_1,
  output [1:0] out_2
);

  wire branch_1_result, button_1_out, clock_1_out, control_unit_1_branch, control_unit_1_load,
       control_unit_1_mem2reg, control_unit_1_op_b_sel, control_unit_1_reg_write, control_unit_1_store;
  wire [1:0] control_unit_1_op_a_sel;
  wire [2:0] rom_1_data_2;
  wire [3:0] control_unit_1_alu_control;
  wire [31:0] alu_1_out_4, I_type, imm_gen_1_out_4, imm_gen_1_out_7, jalr_1_target, multiplexer_1_out,
       multiplexer_2_out, multiplexer_3_out, multiplexer_4_out, multiplexer_5_out, multiplexer_6_out, op_A,
       op_B, PC, PC_4, ram_1_data, rom_1_data, Sb, Uj;

  Clock clock_1 (.out(clock_1_out));
  Register #(.width(32)) register_1 (.D(multiplexer_1_out), .Q(PC), .clk(clock_1_out), .clr(button_1_out));  // open: en
  Button button_1 (.out(button_1_out));
  Multiplexer #(.select(2), .width(32), .enable("false")) multiplexer_1 (
    .in0(PC_4), .in1(Uj), .in2(multiplexer_2_out), .in3(jalr_1_target), .out(multiplexer_1_out), .sel(out_1));
  Adder #(.width(32)) adder_1 (.a(PC), .b(32'h4), .out(PC_4));  // open: cin, cout
  Multiplexer #(.width(32), .enable("false")) multiplexer_2 (
    .in0(PC_4), .in1(Sb), .out(multiplexer_2_out), .sel(branch_1_result));
  branch branch_1 (
    .RESULT(branch_1_result), .in_2(op_B), .in_3(op_A), .func_3(rom_1_data_2), .EN(control_unit_1_branch));
  ROM #(.addrWidth(12), .dataWidth(32)) rom_1 (
    .addr(PC[13:2]), .data({rom_1_data[31:15], rom_1_data_2, rom_1_data[11:0]}));  // open: sel
  imm_gen imm_gen_1 (
    .inst({rom_1_data[31:15], rom_1_data_2, rom_1_data[11:0]}), .PC(PC), .out_3(I_type),
    .out_4(imm_gen_1_out_4), .out_5(Sb), .out_6(Uj), .out_7(imm_gen_1_out_7));
  control_unit control_unit_1 (
    .in_1(rom_1_data[6:0]), .reg_write(control_unit_1_reg_write), .store(control_unit_1_store),
    .load(control_unit_1_load), .op_A_sel(control_unit_1_op_a_sel), .op_B_sel(control_unit_1_op_b_sel),
    .Imm_sel(out_2), .nextPC_sel(out_1), .in_2(rom_1_data_2), .in_3(rom_1_data[30]),
    .mem2reg(control_unit_1_mem2reg), .ALU_control(control_unit_1_alu_control), .branch(control_unit_1_branch));
  reg_file reg_file_1 (
    .A(op_A), .B(op_B), .rd(rom_1_data[11:7]), .reg_enable(control_unit_1_reg_write),
    .write_data(multiplexer_6_out), .rs1(rom_1_data[19:15]), .rs2(rom_1_data[24:20]), .clock(clock_1_out));
  Multiplexer #(.select(2), .width(32), .enable("false")) multiplexer_3 (
    .in0(I_type), .in1(imm_gen_1_out_4), .in2(imm_gen_1_out_7), .out(multiplexer_3_out), .sel(out_2));  // open: in3
  Multiplexer #(.width(32), .enable("false")) multiplexer_4 (
    .in0(op_B), .in1(multiplexer_3_out), .out(multiplexer_4_out), .sel(control_unit_1_op_b_sel));
  Multiplexer #(.select(2), .width(32), .enable("false")) multiplexer_5 (
    .in0(op_A), .in1(PC), .in2(PC_4), .in3({32{1'b0}}), .out(multiplexer_5_out), .sel(control_unit_1_op_a_sel));
  jalr jalr_1 (.rs1(I_type), .imm(op_A), .target(jalr_1_target));
  ALU alu_1 (
    .in_1(multiplexer_5_out), .in_2(multiplexer_4_out), .out_4(alu_1_out_4),
    .data_select(control_unit_1_alu_control));
  RAM #(.addrWidth(12), .dataWidth(32), .bus("separate")) ram_1 (
    .addr(alu_1_out_4[13:2]), .din(op_B), .data(ram_1_data), .str(control_unit_1_store), .clk(clock_1_out),
    .ld(control_unit_1_load), .clr(button_1_out));  // open: sel
  Multiplexer #(.width(32), .enable("false")) multiplexer_6 (
    .in0(ram_1_data), .in1(alu_1_out_4), .out(multiplexer_6_out), .sel(control_unit_1_mem2reg));

  // Other names for the same wires on the sheet: Imm_sel[1:0] = out_2; next_PC[1:0] = out_1

  // Notes on the sheet:
  //   contents of rom_1 (hex, n*v repeats v):
  //   293 128293 502023 2303 4000e7
  //   Khadija
endmodule
